// Logisim project sbc_decode.circ as structural Verilog: 1 circuit, main circuit main
module main (
);

  wire and_1_out, and_2_out, clock_1_out, nand_1_out, nand_2_out, nand_3_out, not_1_out, not_2_out,
       not_3_out, not_4_out, not_5_out;
  wire [3:0] counter_1_q, counter_1_q_2, counter_1_q_3, counter_1_q_4;

  Clock clock_1 (.out(clock_1_out));
  Counter #(.width(16), .max('hffff)) counter_1 (
    .Q({counter_1_q, counter_1_q_2, counter_1_q_3, counter_1_q_4}), .clk(clock_1_out));  // open: load, D, count, carry, clr
  not not_1 (not_1_out, counter_1_q[3]);
  nand nand_1 (nand_1_out, counter_1_q[2], counter_1_q[3]);
  nand nand_2 (nand_2_out, not_1_out, clock_1_out);
  Hex_Digit_Display hex_digit_display_1 (.value(counter_1_q));  // open: dp
  Hex_Digit_Display hex_digit_display_2 (.value(counter_1_q_2));  // open: dp
  LED led_1 (.in(not_2_out));
  not not_2 (not_2_out, nand_2_out);
  not not_3 (not_3_out, nand_1_out);
  LED led_2 (.in(not_3_out));
  Hex_Digit_Display hex_digit_display_3 (.value(counter_1_q_3));  // open: dp
  Hex_Digit_Display hex_digit_display_4 (.value(counter_1_q_4));  // open: dp
  not not_4 (not_4_out, nand_3_out);
  nand nand_3 (nand_3_out, nand_1_out, counter_1_q[3]);
  LED led_3 (.in(and_1_out));
  and and_1 (and_1_out, not_4_out, counter_1_q_3[0]);
  RAM #(.addrWidth(4), .dataWidth(16)) ram_1 (.addr(counter_1_q_4), .sel(and_1_out));  // open: data, clk, ld, clr
  not not_5 (not_5_out, nand_3_out);
  LED led_4 (.in(and_2_out));
  and and_2 (and_2_out, not_5_out, counter_1_q_3[1]);
  RAM #(.addrWidth(4), .dataWidth(16)) ram_2 (.addr(counter_1_q_3), .sel(and_2_out));  // open: data, clk, ld, clr

  // Notes on the sheet:
  //   RAM 0000-7fff
  //   ROM c000-ffff
endmodule
